# Fritzing sketch FritzingSketch (saved by Fritzing 0.9.3b)

parts:
  Componente1 = Arduino Board Ethernet
  VCC1 = Battery
  U1 = Module 4 Relais 5V [package="Module 4 Relais 5V"]
  M1 = DC Motor  # not connected
  M2 = DC Motor  # not connected
  M3 = DC Motor  # not connected
  M5 = DC Motor  # not connected
  Componente2 = Soil Moisture Sensor
  Componente3 = Soil Moisture Sensor
  Componente4 = Soil Moisture Sensor
  Componente5 = Soil Moisture Sensor

nets:
  N1: Componente1.A0, Componente2.SIG
  N2: Componente1.A1, Componente3.SIG
  N3: Componente1.A2, Componente4.SIG
  N4: Componente1.A3, Componente5.SIG
  N5: Componente1.D2_PWM, U1.IN4
  N6: Componente1.D3_PWM, U1.IN3
  N7: Componente1.D4, U1.IN2
  N8: Componente1.D5_PWM, U1.IN1
  GND: VCC1.-, U1.GND, Componente5.GND
  N9: VCC1.+, U1.VCC, U1.K2-NF

custom parts:
  Module 4 Relais 5V: Module 4 Relais 5V 4x SPD-06VDC-SD-C
